// Logisim project 31_05_2019_Ej_1.circ as structural Verilog: 1 circuit, main circuit main
module main (
  input  in_1,
  input  S_1,
  input  S_0,
  input  D_3,
  input  D_2,
  input  D_1,
  input  D_0
);

  wire _0_q, _1_q, _2_q, _3_q, and_1_out, and_2_out, and_3_out, and_4_out, and_5_out, and_6_out, and_7_out,
       and_8_out, and_9_out, and_10_out, and_11_out, and_12_out, and_13_out, and_14_out, and_15_out,
       and_16_out, clock_1_out, not_1_out, not_2_out, not_3_out, not_4_out, not_5_out, not_6_out, or_1_out,
       or_2_out, or_3_out, or_4_out;

  Clock clock_1 (.out(clock_1_out));
  and and_1 (and_1_out, D_3, S_1, S_0);
  not not_1 (not_1_out, S_1);
  not not_2 (not_2_out, S_0);
  not not_3 (not_3_out, _3_q);
  not not_4 (not_4_out, _2_q);
  not not_5 (not_5_out, _1_q);
  not not_6 (not_6_out, _0_q);
  or or_1 (or_1_out, and_1_out, and_2_out, and_3_out, and_5_out);
  and and_2 (and_2_out, not_1_out, not_2_out, _3_q);
  and and_3 (and_3_out, not_1_out, S_0, in_1);
  D_Flip_Flop _3 (.clk(clock_1_out), .D(or_1_out), .Q(_3_q));  // open: Qn, preset, en, reset
  and and_4 (and_4_out, D_2, S_1, S_0);
  and and_5 (and_5_out, S_1, not_2_out, _2_q);
  or or_2 (or_2_out, and_4_out, and_6_out, and_7_out, and_8_out);
  and and_6 (and_6_out, not_1_out, not_2_out, _2_q);
  and and_7 (and_7_out, not_1_out, S_0, _3_q);
  D_Flip_Flop _2 (.clk(clock_1_out), .D(or_2_out), .Q(_2_q));  // open: Qn, preset, en, reset
  and and_8 (and_8_out, S_1, not_2_out, _1_q);
  or or_3 (or_3_out, and_10_out, and_9_out, and_12_out, and_11_out);
  and and_9 (and_9_out, not_1_out, S_0, _2_q);
  and and_10 (and_10_out, not_1_out, not_2_out, _1_q);
  D_Flip_Flop _1 (.clk(clock_1_out), .D(or_3_out), .Q(_1_q));  // open: Qn, preset, en, reset
  and and_11 (and_11_out, S_1, S_0, D_1);
  and and_12 (and_12_out, S_1, not_2_out, _0_q);
  and and_13 (and_13_out, not_1_out, S_0, _1_q);
  and and_14 (and_14_out, not_1_out, not_2_out, _0_q);
  D_Flip_Flop _0 (.clk(clock_1_out), .D(or_4_out), .Q(_0_q));  // open: Qn, preset, en, reset
  or or_4 (or_4_out, and_14_out, and_13_out, and_15_out, and_16_out);
  and and_15 (and_15_out, S_1, not_2_out, in_1);
  and and_16 (and_16_out, S_1, S_0, D_0);
  // Probe on _3_q
  // Probe on _2_q
  // Probe on _1_q
  // Probe on _0_q

  // Notes on the sheet:
  //   3
  //   2
  //   1
  //   0
endmodule
